# Fritzing sketch Sketch (saved by Fritzing 0.9.1b)
breadboards: 1

parts:
  Part1 = Arduino Uno (Rev3)
  Display_On/Off = Pushbutton [package="[THT]"]
  Next_Display = Pushbutton [package="[THT]"]
  R1 = Resistor [tolerance=±5% resistance=10k package=THT]
  R2 = Resistor [tolerance=±5% resistance=10k package=THT]
  LCD_I2C1 = I2C LCD screen
  DHT1 = DHT11 Humitidy and Temperature Sensor

nets:
  N1: Part1.A4/SDA, LCD_I2C1.SDA
  N2: Part1.A5/SCL, LCD_I2C1.SLC
  5V: Part1.D8, Part1.D7, Part1.5V, Display_On/Off.Pin_1, Display_On/Off.Pin_2, Display_On/Off.Pin_3, Display_On/Off.Pin_4, Next_Display.Pin_1, Next_Display.Pin_2, Next_Display.Pin_3, Next_Display.Pin_4, R1.Pin_1, R2.Pin_1, LCD_I2C1.VCC, DHT1.VDD
  N3: Part1.D2, DHT1.DATA
  GND: Part1.GND, R1.Pin_0, R2.Pin_0, LCD_I2C1.GND, DHT1.GND

notes:
  Display On/Off Button
  Next Display Button

custom parts:
  I2C LCD screen: A standard character - with a I2C controller on rear - display, usually with 2x16 characters. Comes in many colors.
  DHT11 Humitidy and Temperature Sensor: DHT11 Humidity and Temperature Sensor
